// Digital circuit part_c_scraps.dig as structural Verilog
module part_c_scraps (
  input  in_a,
  input  in_b,
  input  in_aa,
  input  in_bb,
  input  in_aaa,
  input  in_9,
  input  in_10,
  input  in_12,
  input  in_13,
  input  in_15,
  input  in_17,
  input  in_18,
  input  in_20,
  input  in_21,
  input  in_23,
  input  in_0,
  input  in_1,
  input  in_2,
  input  in_28,
  output out_a,
  output out_aaa,
  output out_aa,
  output out_11,
  output out_14,
  output out_16,
  output out_19,
  output out_22,
  output out_0
);

  wire nfet_1_s, nfet_3_s, nfet_4_s, nfet_6_s, nfet_27_d, nfet_28_d, nfet_38_s, nfet_39_s, pfet_1_d,
       pfet_2_d, pfet_12_d, pfet_14_d, pfet_15_d, pfet_16_d, pfet_17_d, pfet_18_d, pfet_21_d, pfet_22_d,
       pfet_23_d, pfet_24_d, pfet_25_d, pfet_26_d, pfet_27_d, pfet_28_d, pfet_29_d, pfet_30_d, pfet_32_d,
       pfet_33_d, pfet_35_d, pfet_36_d, pfet_37_d, pfet_38_d, undriven, undriven_2;

  PFET pfet_1 (.G(in_9), .S(1'b1), .D(pfet_1_d));
  PFET pfet_2 (.G(in_17), .S(1'b1), .D(pfet_2_d));
  PFET pfet_3 (.G(in_10), .S(1'b1), .D(pfet_1_d));
  NFET nfet_1 (.G(in_9), .D(pfet_1_d), .S(nfet_1_s));
  NFET nfet_2 (.G(in_10), .D(nfet_1_s), .S(1'b0));
  PFET pfet_4 (.G(in_18), .S(1'b1), .D(pfet_2_d));
  NFET nfet_3 (.G(in_17), .D(pfet_2_d), .S(nfet_3_s));
  NFET nfet_4 (.G(in_18), .D(nfet_3_s), .S(nfet_4_s));
  NFET nfet_5 (.G(in_23), .D(nfet_4_s), .S(1'b0));
  PFET pfet_5 (.G(in_a), .S(1'b1), .D(out_a));
  NFET nfet_6 (.G(in_a), .D(out_a), .S(nfet_6_s));
  NFET nfet_7 (.G(in_b), .D(nfet_6_s), .S(1'b0));
  PFET pfet_6 (.G(in_23), .S(1'b1), .D(pfet_2_d));
  PFET pfet_7 (.G(in_b), .S(1'b1), .D(out_a));
  PFET pfet_8 (.G(pfet_1_d), .S(1'b1), .D(out_11));
  NFET nfet_8 (.G(pfet_1_d), .D(out_11), .S(1'b0));
  PFET pfet_9 (.G(pfet_2_d), .S(1'b1), .D(out_19));
  NFET nfet_9 (.G(pfet_2_d), .D(out_19), .S(1'b0));
  PFET pfet_10 (.G(in_aaa), .S(1'b1), .D(out_aaa));
  NFET nfet_10 (.G(in_aaa), .D(out_aaa), .S(1'b0));
  PFET pfet_11 (.G(in_15), .S(1'b1), .D(out_16));
  NFET nfet_11 (.G(in_15), .D(out_16), .S(1'b0));
  PFET pfet_12 (.G(in_bb), .S(1'b1), .D(pfet_12_d));
  PFET pfet_13 (.G(in_aa), .S(pfet_12_d), .D(out_aa));
  NFET nfet_12 (.G(in_aa), .D(out_aa), .S(1'b0));
  NFET nfet_13 (.G(in_bb), .D(out_aa), .S(1'b0));
  PFET pfet_14 (.G(in_13), .S(1'b1), .D(pfet_14_d));
  PFET pfet_15 (.G(in_12), .S(pfet_14_d), .D(pfet_15_d));
  NFET nfet_14 (.G(in_12), .D(pfet_15_d), .S(1'b0));
  PFET pfet_16 (.G(in_28), .S(1'b1), .D(pfet_16_d));
  PFET pfet_17 (.G(in_21), .S(pfet_16_d), .D(pfet_17_d));
  PFET pfet_18 (.G(in_20), .S(pfet_17_d), .D(pfet_18_d));
  NFET nfet_15 (.G(in_20), .D(pfet_18_d), .S(1'b0));
  NFET nfet_16 (.G(in_13), .D(pfet_15_d), .S(1'b0));
  NFET nfet_17 (.G(in_21), .D(pfet_18_d), .S(1'b0));
  NFET nfet_18 (.G(in_28), .D(pfet_18_d), .S(1'b0));
  PFET pfet_19 (.G(pfet_15_d), .S(1'b1), .D(out_14));
  NFET nfet_19 (.G(pfet_15_d), .D(out_14), .S(1'b0));
  PFET pfet_20 (.G(pfet_18_d), .S(1'b1), .D(out_22));
  NFET nfet_20 (.G(pfet_18_d), .D(out_22), .S(1'b0));
  PFET pfet_21 (.G(in_2), .S(1'b1), .D(pfet_21_d));
  NFET nfet_21 (.G(in_2), .D(pfet_21_d), .S(1'b0));
  PFET pfet_22 (.G(in_1), .S(1'b1), .D(pfet_22_d));
  NFET nfet_22 (.G(in_1), .D(pfet_22_d), .S(1'b0));
  PFET pfet_23 (.G(in_2), .S(1'b1), .D(pfet_23_d));
  NFET nfet_23 (.G(in_2), .D(pfet_23_d), .S(1'b0));
  PFET pfet_24 (.G(in_0), .S(1'b1), .D(pfet_24_d));
  NFET nfet_24 (.G(in_0), .D(pfet_24_d), .S(1'b0));
  PFET pfet_25 (.G(in_1), .S(1'b1), .D(pfet_25_d));
  NFET nfet_25 (.G(in_1), .D(pfet_25_d), .S(1'b0));
  PFET pfet_26 (.G(pfet_21_d), .S(1'b1), .D(pfet_26_d));
  PFET pfet_27 (.G(in_1), .S(pfet_26_d), .D(pfet_27_d));
  PFET pfet_28 (.G(in_0), .S(pfet_27_d), .D(pfet_28_d));
  NFET nfet_26 (.G(in_0), .D(pfet_28_d), .S(1'b0));
  NFET nfet_27 (.G(pfet_23_d), .D(nfet_27_d), .S(1'b0));
  NFET nfet_28 (.G(undriven), .D(nfet_28_d), .S(1'b0));
  NFET nfet_29 (.G(in_1), .D(pfet_28_d), .S(1'b0));
  PFET pfet_29 (.G(in_0), .S(1'b1), .D(pfet_29_d));
  PFET pfet_30 (.G(pfet_22_d), .S(pfet_29_d), .D(pfet_30_d));
  PFET pfet_31 (.G(pfet_23_d), .S(pfet_30_d), .D(nfet_27_d));
  NFET nfet_30 (.G(pfet_22_d), .D(nfet_27_d), .S(1'b0));
  PFET pfet_32 (.G(pfet_24_d), .S(1'b1), .D(pfet_32_d));
  PFET pfet_33 (.G(pfet_25_d), .S(pfet_32_d), .D(pfet_33_d));
  PFET pfet_34 (.G(undriven), .S(pfet_33_d), .D(nfet_28_d));
  NFET nfet_31 (.G(pfet_21_d), .D(pfet_28_d), .S(1'b0));
  NFET nfet_32 (.G(in_0), .D(nfet_27_d), .S(1'b0));
  NFET nfet_33 (.G(pfet_25_d), .D(nfet_28_d), .S(1'b0));
  NFET nfet_34 (.G(pfet_24_d), .D(nfet_28_d), .S(1'b0));
  PFET pfet_35 (.G(pfet_28_d), .S(1'b1), .D(pfet_35_d));
  NFET nfet_35 (.G(pfet_28_d), .D(pfet_35_d), .S(1'b0));
  PFET pfet_36 (.G(nfet_27_d), .S(1'b1), .D(pfet_36_d));
  NFET nfet_36 (.G(nfet_27_d), .D(pfet_36_d), .S(1'b0));
  PFET pfet_37 (.G(nfet_28_d), .S(1'b1), .D(pfet_37_d));
  NFET nfet_37 (.G(nfet_28_d), .D(pfet_37_d), .S(1'b0));
  PFET pfet_38 (.G(pfet_35_d), .S(1'b1), .D(pfet_38_d));
  PFET pfet_39 (.G(undriven_2), .S(1'b1), .D(pfet_38_d));
  NFET nfet_38 (.G(pfet_35_d), .D(pfet_38_d), .S(nfet_38_s));
  NFET nfet_39 (.G(undriven_2), .D(nfet_38_s), .S(nfet_39_s));
  NFET nfet_40 (.G(pfet_37_d), .D(nfet_39_s), .S(1'b0));
  PFET pfet_40 (.G(pfet_37_d), .S(1'b1), .D(pfet_38_d));
  PFET pfet_41 (.G(pfet_38_d), .S(1'b1), .D(out_0));
  NFET nfet_41 (.G(pfet_38_d), .D(out_0), .S(1'b0));

  // Notes on the sheet:
  //   AND
  //   AND (3)
  //   NAND
  //   NOT
  //   NOR
  //   OR
  //   OR (3)
endmodule

/* Test case nand test:
in_a in_b out_a
1 1 0
1 0 1
0 1 1
0 0 1
*/

/* Test case or test:
in_aaa out_aaa
1 0
0 1
*/

/* Test case nor test:
in_aa in_bb out_aa
1 1 0
1 0 0
0 1 0
0 0 1
*/

/* Test case test_c:
in_0 in_1 in_2 out_0
0 0 0 1
0 0 1 0
0 1 0 1
0 1 1 0
1 0 0 1
1 0 1 1
1 1 0 0
1 1 1 1
*/
