// Digital circuit lab2_part2.dig as structural Verilog
module lab2_part2 (
  input  in0,
  input  in1,
  input  in2,
  input  in3,
  output seg_a,
  output seg_f,
  output seg_b,
  output seg_g,
  output seg_e,
  output seg_c,
  output seg_d,
  output seg_dp,
  output sign_a,
  output sign_f,
  output sign_b,
  output sign_g,
  output sign_e,
  output sign_c,
  output sign_d,
  output sign_dp
);

  Seven_Seg seven_seg_1 (.a(1'b0), .b(1'b0), .c(1'b0), .d(1'b0), .e(1'b0), .f(1'b0), .g(in3), .dp(1'b0));
  Seven_Seg seven_seg_2 (.a(seg_a), .b(seg_b), .c(seg_c), .d(seg_d), .e(seg_e), .f(seg_f), .g(seg_g), .dp(1'b0));
  Multiplexer #(.Selector_Bits(4)) multiplexer_1 (
    .sel({in3, in2, in1, in0}), .in_0(1'b1), .in_1(1'b0), .in_2(1'b1), .in_3(1'b1), .in_4(1'b0), .in_5(1'b1),
    .in_6(1'b1), .in_7(1'b1), .in_8(1'b1), .in_9(1'b1), .in_10(1'b1), .in_11(1'b1), .in_12(1'b0),
    .in_13(1'b1), .in_14(1'b1), .in_15(1'b0), .out(seg_a));
  Multiplexer #(.Selector_Bits(4)) multiplexer_2 (
    .sel({in3, in2, in1, in0}), .in_0(1'b1), .in_1(1'b0), .in_2(1'b1), .in_3(1'b0), .in_4(1'b0), .in_5(1'b0),
    .in_6(1'b1), .in_7(1'b0), .in_8(1'b1), .in_9(1'b0), .in_10(1'b1), .in_11(1'b0), .in_12(1'b0),
    .in_13(1'b0), .in_14(1'b1), .in_15(1'b0), .out(seg_e));
  Multiplexer #(.Selector_Bits(4)) multiplexer_3 (
    .sel({in3, in2, in1, in0}), .in_0(1'b1), .in_1(1'b1), .in_2(1'b1), .in_3(1'b1), .in_4(1'b1), .in_5(1'b0),
    .in_6(1'b0), .in_7(1'b1), .in_8(1'b1), .in_9(1'b1), .in_10(1'b0), .in_11(1'b0), .in_12(1'b1),
    .in_13(1'b1), .in_14(1'b1), .in_15(1'b1), .out(seg_b));
  Multiplexer #(.Selector_Bits(4)) multiplexer_4 (
    .sel({in3, in2, in1, in0}), .in_0(1'b1), .in_1(1'b0), .in_2(1'b0), .in_3(1'b0), .in_4(1'b1), .in_5(1'b1),
    .in_6(1'b1), .in_7(1'b0), .in_8(1'b1), .in_9(1'b0), .in_10(1'b1), .in_11(1'b1), .in_12(1'b1),
    .in_13(1'b0), .in_14(1'b0), .in_15(1'b0), .out(seg_f));
  Multiplexer #(.Selector_Bits(4)) multiplexer_5 (
    .sel({in3, in2, in1, in0}), .in_0(1'b0), .in_1(1'b0), .in_2(1'b1), .in_3(1'b1), .in_4(1'b1), .in_5(1'b1),
    .in_6(1'b1), .in_7(1'b0), .in_8(1'b1), .in_9(1'b0), .in_10(1'b1), .in_11(1'b1), .in_12(1'b1),
    .in_13(1'b1), .in_14(1'b1), .in_15(1'b0), .out(seg_g));
  Multiplexer #(.Selector_Bits(4)) multiplexer_6 (
    .sel({in3, in2, in1, in0}), .in_0(1'b1), .in_1(1'b1), .in_2(1'b0), .in_3(1'b1), .in_4(1'b1), .in_5(1'b1),
    .in_6(1'b1), .in_7(1'b1), .in_8(1'b1), .in_9(1'b1), .in_10(1'b1), .in_11(1'b1), .in_12(1'b1),
    .in_13(1'b1), .in_14(1'b0), .in_15(1'b1), .out(seg_c));
  Multiplexer #(.Selector_Bits(4)) multiplexer_7 (
    .sel({in3, in2, in1, in0}), .in_0(1'b1), .in_1(1'b0), .in_2(1'b1), .in_3(1'b1), .in_4(1'b0), .in_5(1'b1),
    .in_6(1'b1), .in_7(1'b0), .in_8(1'b1), .in_9(1'b0), .in_10(1'b1), .in_11(1'b1), .in_12(1'b0),
    .in_13(1'b1), .in_14(1'b1), .in_15(1'b0), .out(seg_d));

  assign seg_dp = 1'b0;
  assign sign_a = 1'b0;
  assign sign_b = 1'b0;
  assign sign_c = 1'b0;
  assign sign_d = 1'b0;
  assign sign_dp = 1'b0;
  assign sign_e = 1'b0;
  assign sign_f = 1'b0;
  assign sign_g = in3;

  // Notes on the sheet:
  //   Interface (do not edit the content inside this box)
  //   Outputs:
  //   Inputs
  //   Sign
  //   Decimal Number
  //   seg_a
  //   seg_e
  //   seg_b
  //   seg_f
  //   seg_g
  //   seg_c
  //   seg_d
endmodule

/* Test case:
in3 in2 in1 in0  sign_a sign_b sign_c sign_d sign_e sign_f sign_g  seg_a seg_b seg_c seg_d seg_e seg_f seg_g
 0   0   0   0    0      0      0      0      0      0      0       1     1     1     1     1     1     0
*/
