// Digital circuit lab2_part2_v1.dig as structural Verilog
module lab2_part2_v1 (
  input  in0,
  input  in1,
  input  in2,
  input  in3,
  output seg_a,
  output seg_f,
  output seg_b,
  output seg_g,
  output seg_e,
  output seg_c,
  output seg_d,
  output seg_dp,
  output sign_a,
  output sign_f,
  output sign_b,
  output sign_g,
  output sign_e,
  output sign_c,
  output sign_d,
  output sign_dp
);

  wire not_1_out, not_2_out, not_3_out, not_5_out, not_6_out, not_7_out;

  Seven_Seg seven_seg_1 (.a(sign_a), .b(sign_b), .c(sign_c), .d(sign_d), .e(sign_e), .f(sign_f), .g(in3), .dp(1'b0));
  Seven_Seg seven_seg_2 (.a(seg_a), .b(seg_a), .c(seg_a), .d(seg_a), .e(seg_a), .f(seg_a), .g(seg_a), .dp(1'b0));
  not not_1 (not_1_out, in2);
  not not_2 (not_2_out, in0);
  not not_3 (not_3_out, in1);
  and and_1 (seg_a, not_1_out, not_2_out, not_3_out);
  and and_2 (seg_a, in2, in0, in1);
  not not_4 (seg_a, seg_a);
  not not_5 (not_5_out, in2);
  not not_6 (not_6_out, in1);
  not not_7 (not_7_out, in1);
  and and_3 (seg_a, not_5_out, in0, not_6_out);
  and and_4 (seg_a, in2, in0, not_7_out);
  not not_8 (seg_a, seg_a);
  not not_9 (seg_a, seg_a);

  assign seg_b = seg_a;
  assign seg_c = seg_a;
  assign seg_d = seg_a;
  assign seg_dp = 1'b0;
  assign seg_e = seg_a;
  assign seg_f = seg_a;
  assign seg_g = seg_a;
  assign sign_dp = 1'b0;
  assign sign_g = in3;

  // Notes on the sheet:
  //   Interface (do not edit the content inside this box)
  //   Outputs:
  //   Inputs
  //   Sign
  //   Decimal Number
  //   1
  //   2
endmodule

/* Test case:
in3 in2 in1 in0  sign_a sign_b sign_c sign_d sign_e sign_f sign_g  seg_a seg_b seg_c seg_d seg_e seg_f seg_g
 0   0   0   0    0      0      0      0      0      0      0       1     1     1     1     1     1     0
*/
