// Digital circuit lab2_part3_92percent.dig as structural Verilog
module lab2_part3_92percent (
  input  clk,
  input  in0,
  input  in1,
  input  in2,
  input  in3,
  input  sel_write_1,
  input  sel_write_0,
  input  sel_readA_1,
  input  sel_readA_0,
  input  sel_readB_1,
  input  sel_readB_0,
  output out0,
  output out1,
  output out2,
  output out3,
  output reg0_0,
  output reg0_1,
  output reg0_2,
  output reg0_3,
  output reg1_0,
  output reg1_1,
  output reg1_2,
  output reg1_3,
  output reg2_0,
  output reg2_1,
  output reg2_2,
  output reg2_3,
  output reg3_0,
  output reg3_1,
  output reg3_2,
  output reg3_3,
  output inA_0,
  output inA_1,
  output inA_2,
  output inA_3,
  output inB_0,
  output inB_1,
  output inB_2,
  output inB_3
);

  wire multiplexer_1_out, multiplexer_2_out, multiplexer_3_out, multiplexer_4_out;
  wire [3:0] multiplexer_7_out, multiplexer_8_out;

  Multiplexer #(.Selector_Bits(2)) multiplexer_1 (
    .sel({sel_write_1, sel_write_0}), .in_0(1'b1), .in_1(1'b0), .in_2(1'b0), .in_3(1'b0),
    .out(multiplexer_1_out));
  Multiplexer #(.Selector_Bits(2)) multiplexer_2 (
    .sel({sel_write_1, sel_write_0}), .in_0(1'b0), .in_1(1'b1), .in_2(1'b0), .in_3(1'b0),
    .out(multiplexer_2_out));
  Multiplexer #(.Selector_Bits(2)) multiplexer_3 (
    .sel({sel_write_1, sel_write_0}), .in_0(1'b0), .in_1(1'b0), .in_2(1'b1), .in_3(1'b0),
    .out(multiplexer_3_out));
  Multiplexer #(.Selector_Bits(2)) multiplexer_4 (
    .sel({sel_write_1, sel_write_0}), .in_0(1'b0), .in_1(1'b0), .in_2(1'b0), .in_3(1'b1),
    .out(multiplexer_4_out));
  Register #(.Bits(4)) register_1 (
    .D({in3, in2, in1, in0}), .C(clk), .en(multiplexer_1_out), .Q({reg0_3, reg0_2, reg0_1, reg0_0}));
  Register #(.Bits(4)) register_2 (
    .D({in3, in2, in1, in0}), .C(clk), .en(multiplexer_2_out), .Q({reg1_3, reg1_2, reg1_1, reg1_0}));
  Register #(.Bits(4)) register_3 (
    .D({in3, in2, in1, in0}), .C(clk), .en(multiplexer_3_out), .Q({reg2_3, reg2_2, reg2_1, reg2_0}));
  Register #(.Bits(4)) register_4 (
    .D({in3, in2, in1, in0}), .C(clk), .en(multiplexer_4_out), .Q({reg3_3, reg3_2, reg3_1, reg3_0}));
  Seven_Seg_Hex seven_seg_hex_1 (.d({inA_3, inA_2, inA_1, inA_0}), .dp(1'b0));
  Seven_Seg_Hex seven_seg_hex_2 (.d({reg3_3, reg3_2, reg3_1, reg3_0}), .dp(1'b0));
  Seven_Seg_Hex seven_seg_hex_3 (.d({in3, in2, in1, in0}), .dp(1'b0));
  Seven_Seg_Hex seven_seg_hex_4 (.d({inB_3, inB_2, inB_1, inB_0}), .dp(1'b0));
  Seven_Seg_Hex seven_seg_hex_5 (.d({reg2_3, reg2_2, reg2_1, reg2_0}), .dp(1'b0));
  Seven_Seg_Hex seven_seg_hex_6 (.d({2'b00, sel_write_1, sel_write_0}), .dp(1'b0));
  Seven_Seg_Hex seven_seg_hex_7 (.d({2'b00, sel_readA_1, sel_readA_0}), .dp(1'b0));
  Seven_Seg_Hex seven_seg_hex_8 (.d({out3, out2, out1, out0}), .dp(1'b0));
  Seven_Seg_Hex seven_seg_hex_9 (.d({reg1_3, reg1_2, reg1_1, reg1_0}), .dp(1'b0));
  Seven_Seg_Hex seven_seg_hex_10 (.d({2'b00, sel_readB_1, sel_readB_0}), .dp(1'b0));
  Seven_Seg_Hex seven_seg_hex_11 (.d({reg0_3, reg0_2, reg0_1, reg0_0}), .dp(1'b0));
  Multiplexer #(.Selector_Bits(2)) multiplexer_5 (
    .sel({inB_1, inB_0}), .in_0(inA_0), .in_1(inA_3), .in_2(inA_2), .in_3(inA_1), .out(out0));
  Multiplexer #(.Selector_Bits(2)) multiplexer_6 (
    .sel({inB_1, inB_0}), .in_0(inA_1), .in_1(inA_0), .in_2(inA_3), .in_3(inA_2), .out(out1));
  Multiplexer #(.Selector_Bits(2), .Bits(4)) multiplexer_7 (
    .sel({sel_readA_1, sel_readA_0}), .in_0({reg0_3, reg0_2, reg0_1, reg0_0}),
    .in_1({reg1_3, reg1_2, reg1_1, reg1_0}), .in_2({reg2_3, reg2_2, reg2_1, reg2_0}),
    .in_3({reg3_3, reg3_2, reg3_1, reg3_0}), .out(multiplexer_7_out));
  Multiplexer #(.Selector_Bits(2), .Bits(4)) multiplexer_8 (
    .sel({sel_readB_1, sel_readB_0}), .in_0({reg0_3, reg0_2, reg0_1, reg0_0}),
    .in_1({reg1_3, reg1_2, reg1_1, reg1_0}), .in_2({reg2_3, reg2_2, reg2_1, reg2_0}),
    .in_3({reg3_3, reg3_2, reg3_1, reg3_0}), .out(multiplexer_8_out));
  Register #(.Bits(4)) register_5 (.D(multiplexer_7_out), .C(clk), .en(1'b1), .Q({inA_3, inA_2, inA_1, inA_0}));
  Register #(.Bits(4)) register_6 (.D(multiplexer_8_out), .C(clk), .en(1'b1), .Q({inB_3, inB_2, inB_1, inB_0}));
  Multiplexer #(.Selector_Bits(2)) multiplexer_9 (
    .sel({inB_1, inB_0}), .in_0(inA_2), .in_1(inA_1), .in_2(inA_0), .in_3(inA_3), .out(out2));
  Multiplexer #(.Selector_Bits(2)) multiplexer_10 (
    .sel({inB_1, inB_0}), .in_0(inA_3), .in_1(inA_2), .in_2(inA_1), .in_3(inA_0), .out(out3));

  // Other names for the same wires on the sheet: reg0[3:0] = {reg0_3, reg0_2, reg0_1, reg0_0};
  //   reg1[3:0] = {reg1_3, reg1_2, reg1_1, reg1_0}; reg2[3:0] = {reg2_3, reg2_2, reg2_1, reg2_0};
  //   reg3[3:0] = {reg3_3, reg3_2, reg3_1, reg3_0}

  // Notes on the sheet:
  //   Register 0
  //   Register 1
  //   Register 2
  //   Register 3
  //   Interface (do not edit the content inside this box)
  //   Inputs
  //   Keypad
  //   Outputs
  //   Registers
  //   Values read into ALU inputs
  //   Rotatee
  //   Synchronizing Clock
  //   Rotation amount:
  //   Register Selection: Write-to
  //   Register Selection: Read-from
  //   ALU Output
  //   ALU input A register address:
  //   ALU input B register address:
  //   out_0
  //   out_1
  //   ALU input: rotatee
  //   ALU input: rotation amount
  //   out_2
  //   out_3
endmodule

/* Test case:
clk in3 in2 in1 in0 sel^write_1 sel^write_0 sel^readA_1 sel^readA_0 sel^readB_1 sel^readB_0  reg3_3 reg3_2 reg3_1 reg3_0 reg2_3 reg2_2 reg2_1 reg2_0 reg1_3 reg1_2 reg1_1 reg1_0 reg0_3 reg0_2 reg0_1 reg0_0 out3 out2 out1 out0
 0   0   0   0   0   0           0           0           0           0           0            0      0      0      0      0      0      0      0      0      0      0      0      0      0      0      0      0    0    0    0
 1   0   0   0   0   0           0           0           0           0           0            0      0      0      0      0      0      0      0      0      0      0      0      0      0      0      0      0    0    0    0
 0   0   1   0   1   1           1           0           0           0           0            0      0      0      0      0      0      0      0      0      0      0      0      0      0      0      0      0    0    0    0
 1   0   1   0   1   1           1           0           0           0           0            0      1      0      1      0      0      0      0      0      0      0      0      0      0      0      0      0    0    0    0
 0   0   0   0   1   0           1           0           0           0           0            0      1      0      1      0      0      0      0      0      0      0      0      0      0      0      0      0    0    0    0
 1   0   0   0   1   0           1           0           0           0           0            0      1      0      1      0      0      0      0      0      0      0      1      0      0      0      0      0    0    0    0
 0   0   0   0   0   0           0           1           1           0           1            0      1      0      1      0      0      0      0      0      0      0      1      0      0      0      0      1    0    1    0
 1   0   0   0   0   0           0           1           1           0           1            0      1      0      1      0      0      0      0      0      0      0      1      0      0      0      0      1    0    1    0
 0   0   0   0   0   0           0           0           1           1           1            0      1      0      1      0      0      0      0      0      0      0      1      0      0      0      0      0    0    1    0
 1   0   0   0   0   0           0           0           1           1           1            0      1      0      1      0      0      0      0      0      0      0      1      0      0      0      0      0    0    1    0
*/
