// Digital circuit lab2_part2_practice.dig as structural Verilog
module lab2_part2_practice (
  input  in0,
  input  in1,
  input  in2,
  input  in3,
  output seg_a,
  output seg_f,
  output seg_b,
  output seg_g,
  output seg_e,
  output seg_c,
  output seg_d,
  output seg_dp,
  output sign_a,
  output sign_f,
  output sign_b,
  output sign_g,
  output sign_e,
  output sign_c,
  output sign_d,
  output sign_dp
);

  Seven_Seg seven_seg_1 (.a(in2), .b(in1), .c(in0), .d(in2), .e(in0), .f(in1), .g(in3), .dp(in0));
  Seven_Seg seven_seg_2 (.a(in2), .b(in1), .c(in0), .d(in2), .e(in0), .f(in1), .g(in0), .dp(in0));

  assign seg_a = in2;
  assign seg_b = in1;
  assign seg_c = in0;
  assign seg_d = in2;
  assign seg_dp = in0;
  assign seg_e = in0;
  assign seg_f = in1;
  assign seg_g = in0;
  assign sign_a = in2;
  assign sign_b = in1;
  assign sign_c = in0;
  assign sign_d = in2;
  assign sign_dp = in0;
  assign sign_e = in0;
  assign sign_f = in1;
  assign sign_g = in3;

  // Notes on the sheet:
  //   Interface (do not edit the content inside this box)
  //   Outputs:
  //   Inputs
  //   Sign
  //   Decimal Number
endmodule

/* Test case:
in3 in2 in1 in0  sign_a sign_b sign_c sign_d sign_e sign_f sign_g  seg_a seg_b seg_c seg_d seg_e seg_f seg_g
 0   0   0   0    0      0      0      0      0      0      0       1     1     1     1     1     1     0
*/
